# Fritzing sketch BAIT (saved by Fritzing 0.9.4)

parts:
  Teensy1 = Teensy 3.6 (Basic)
  Part1 = Adafruit I2S Mic - SPH0645 [part_number="Adafruit #3421"]
  Part2 = Adafruit TSL2561 [part_number="Adafruit #439"]
  Part3 = Adafruit Si7021 Temp Humidity [part_number="Adafruit #3251"]
  Part4 = PowerBoost 500 Basic
  Part5 = Adafruit USB DC Solar LiPo Charger [part_number="Adafruit #390"]
  R1 = Resistor [tolerance=±5% resistance=22k package="0402 [SMD]"]
  U1 = SWITCH-SPST-2 [package=switch-spst-vertical]
  BAT1 = Battery Holders [package=battcom_20mm_pth]  # not connected
  R2 = Resistor [tolerance=±5% resistance=22k package="0402 [SMD]"]

nets:
  GND: Teensy1.GND, Teensy1.GND1, Part1.GND, Part2.GND, Part3.GND, Part4.GND, Part5.GND, R1.Pin_0, U1.O
  N1: Teensy1.D13, Part1.DATA
  N2: Teensy1.A4/D18, Part2.SDA, Part3.SDA
  N3: Teensy1.A5/D19, Part2.SCL, Part3.SCL
  N4: Teensy1.A9/D23, Part1.WS
  3V3: Teensy1.3V3, Teensy1.3V3_1, Part1.VDD, Part2.3.3V, Part3.+3V3
  N5: Teensy1.Vin, Part4.5.0V
  N6: Teensy1.D36, R1.Pin_1, R2.Pin_0
  N7: Part4.VBAT, Part5.LOAD
  N8: Part4.ENABLE, U1.P
  N9: Part5.BATT, R2.Pin_1

custom parts:
  Teensy 3.6 (Basic): The Teensy is a complete USB-based microcontoller development system, in a very small footprint, capable of implementing many types of projects. All programming is done via the USB port. No special programmer is needed, only a standard micro-USB cable and a PC or Macintosh with a USB port.
  Adafruit I2S Mic - SPH0645: For many microcontrollers, adding audio input is easy with one of our analog microphone breakouts. But as you get to bigger and better microcontrollers and microcomputers, you'll find that you don't always have an analog input, or maybe you want to avoid the noise that can seep in with an analog mic system. Once you get past 8-bit micros, you will often find an I2S peripheral, that can take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
  Adafruit TSL2561: The TSL2561 luminosity sensor is an advanced digital light sensor, ideal for use in a wide range of light situations. Compared to low cost CdS cells, this sensor is more precise, allowing for exact lux calculations and can be configured for different gain/timing ranges to detect light ranges from up to 0.1 - 40,000+ Lux on the fly. The best part of this sensor is that it contains both infrared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
  Adafruit Si7021 Temp Humidity: It's summer and you're sweating and your hair's all frizzy and all you really want to know is why the weatherman said this morning that today's relative humidity would max out at a perfectly reasonable 42% when it feels more like 77%. Enter the Si7021 Temperature + Humidity Sensor - the best way to prove the weatherman wrong! This lovely sensor for Silicon labs has ± 3% relative humidity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
  PowerBoost 500 Basic: The PowerBoost 500 Basic is a little DC/DC boost converter module that can run from 1.8V batteries or higher, and convert the battery output to 5.2V DC for running your 5V projects. At its heart is a TPS61090 boost converter from TI. This boost converter chip has some really nice extras such as low battery detection, 2A internal switch, synchronous conversion, excellent efficiency, and 700KHz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
  Adafruit USB DC Solar LiPo Charger: Make your projects to go green this summer with our specialized USB/Solar Lithium Ion Polymer Battery charger! This charger is a very unique design, perfect for outdoor projects, or DIY iPod chargers. We've spent over a year testing and tinkering with this charger to come up with a plug and play solution to charging batteries with the sun and we're really pleased with what we ended up with.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
